# Fritzing sketch Citizension-Smart-Kozani-IoT-System (saved by Fritzing 0.9.3b)
breadboards: 1

parts:
  Εξάρτημα1 = Adafruit MAX9814 Electret Microphone Amplifier [part_number="Adafruit #1713"]
  Εξάρτημα2 = Adafruit CCS811
  Εξάρτημα3 = Arduino Uno (Rev3) - ICSP
  Εξάρτημα4 = Arduino Ethernet Shield (Rev3)  # not connected

nets:
  GND: Εξάρτημα1.GND, Εξάρτημα2.GND, Εξάρτημα3.GND
  VDD: Εξάρτημα1.VDD, Εξάρτημα1.GAIN, Εξάρτημα3.3V3
  N1: Εξάρτημα1.OUTPUT, Εξάρτημα3.A1
  VIN: Εξάρτημα2.VIN, Εξάρτημα3.5V
  N2: Εξάρτημα2.SDA, Εξάρτημα3.A4/SDA
  N3: Εξάρτημα2.SCL, Εξάρτημα3.A5/SCL

notes:
  5v
  3.3V

custom parts:
  Adafruit MAX9814 Electret Microphone Amplifier: Add an ear to your project with this well-designed electret microphone amplifier with AGC. This fully assembled and tested board comes with a 20-20KHz electret microphone soldered on. For the amplification, we use the Maxim MAX9814, a specialty chip that is designed for amplifying electret microphones in situations where the loudness of the audio isn't predictable. This fancy microphone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
